// Logisim project 8 bit alu.circ as structural Verilog: 8 circuits, main circuit main
module main (
  input  [2:0] OP,
  input  [7:0] A,
  input  [7:0] B,
  output zero,
  output overflow,
  output carry,
  output negative,
  output [7:0] out
);

  wire [7:0] add_sub_1_out, and_1_out, not_1_out, or_1_out, xor_1_out;

  ADD_SUB add_sub_1 (
    .zero(zero), .out(add_sub_1_out), .negative(negative), .overflow(overflow), .carry(carry), .A(A), .B(B),
    .op(OP[0]));
  assign not_1_out = ~A;  // NOT_Gate not_1, 8 bits wide
  assign and_1_out = A & B;  // AND_Gate and_1, 8 bits wide
  assign or_1_out = A | B;  // OR_Gate or_1, 8 bits wide
  assign xor_1_out = A ^ B;  // XOR_Gate xor_1, 8 bits wide
  _8_3_bit_mux u_8_3_bit_mux_1 (
    .in_4(add_sub_1_out), .in_5(add_sub_1_out), .in_6(not_1_out), .in_7(and_1_out), .in_8(or_1_out),
    .in_9(xor_1_out), .in_10({1'b0, A[7:1]}), .in_11({A[6:0], 1'b0}), .out_12(out), .in_1(OP[0]),
    .in_2(OP[1]), .in_3(OP[2]));
endmodule

module full_adder (
  input  in_1,
  input  in_2,
  input  in_3,
  output out_4,
  output out_5
);

  wire and_1_out, and_2_out, xor_1_out;

  xor xor_1 (xor_1_out, in_1, in_2);
  xor xor_2 (out_4, xor_1_out, in_3);
  and and_1 (and_1_out, xor_1_out, in_3);
  and and_2 (and_2_out, in_1, in_2);
  or or_1 (out_5, and_1_out, and_2_out);
endmodule

module ADD_SUB (
  input  [7:0] B,
  input  op,
  input  [7:0] A,
  output zero,
  output [7:0] out,
  output negative,
  output overflow,
  output carry
);

  wire and_1_out, and_2_out, not_1_out, not_2_out, not_3_out;
  wire [7:0] xor_1_out;

  assign xor_1_out = B ^ {8{op}};  // XOR_Gate xor_1, 8 bits wide
  _8_bit_adder u_8_bit_adder_1 (
    .in_2(xor_1_out[0]), .in_3(xor_1_out[1]), .in_4(xor_1_out[2]), .in_5(xor_1_out[3]), .in_6(xor_1_out[4]),
    .in_7(xor_1_out[5]), .in_8(xor_1_out[6]), .in_9(xor_1_out[7]), .in_10(A[0]), .in_11(A[1]), .in_12(A[2]),
    .in_13(A[3]), .in_14(A[4]), .in_15(A[5]), .in_16(A[6]), .in_17(A[7]), .out_18(out[0]), .out_19(out[1]),
    .out_20(out[2]), .out_21(out[3]), .out_22(out[4]), .out_23(out[5]), .out_24(out[6]), .out_25(negative),
    .out_26(carry), .in_1(op));
  not not_1 (not_1_out, A[7]);
  not not_2 (not_2_out, negative);
  and and_1 (and_1_out, not_1_out, negative, not_3_out);
  not not_3 (not_3_out, xor_1_out[7]);
  and and_2 (and_2_out, A[7], not_2_out, xor_1_out[7]);
  nor nor_1 (zero, out[0], out[1], out[2], out[3], out[4], out[5], out[6], negative);
  or or_1 (overflow, and_1_out, and_2_out);

  assign out[7] = negative;
endmodule

module _8_bit_adder (
  input  in_1,
  input  in_2,
  input  in_3,
  input  in_4,
  input  in_5,
  input  in_6,
  input  in_7,
  input  in_8,
  input  in_9,
  input  in_10,
  input  in_11,
  input  in_12,
  input  in_13,
  input  in_14,
  input  in_15,
  input  in_16,
  input  in_17,
  output out_18,
  output out_19,
  output out_20,
  output out_21,
  output out_22,
  output out_23,
  output out_24,
  output out_25,
  output out_26
);

  wire full_adder_1_out_5, full_adder_2_out_5, full_adder_3_out_5, full_adder_4_out_5, full_adder_5_out_5,
       full_adder_6_out_5, full_adder_7_out_5;

  full_adder full_adder_1 (.in_1(in_2), .in_2(in_10), .in_3(in_1), .out_4(out_18), .out_5(full_adder_1_out_5));
  full_adder full_adder_2 (
    .in_1(in_3), .in_2(in_11), .in_3(full_adder_1_out_5), .out_4(out_19), .out_5(full_adder_2_out_5));
  full_adder full_adder_3 (
    .in_1(in_4), .in_2(in_12), .in_3(full_adder_2_out_5), .out_4(out_20), .out_5(full_adder_3_out_5));
  full_adder full_adder_4 (
    .in_1(in_5), .in_2(in_13), .in_3(full_adder_3_out_5), .out_4(out_21), .out_5(full_adder_4_out_5));
  full_adder full_adder_5 (
    .in_1(in_6), .in_2(in_14), .in_3(full_adder_4_out_5), .out_4(out_22), .out_5(full_adder_5_out_5));
  full_adder full_adder_6 (
    .in_1(in_7), .in_2(in_15), .in_3(full_adder_5_out_5), .out_4(out_23), .out_5(full_adder_6_out_5));
  full_adder full_adder_7 (
    .in_1(in_8), .in_2(in_16), .in_3(full_adder_6_out_5), .out_4(out_24), .out_5(full_adder_7_out_5));
  full_adder full_adder_8 (.in_1(in_9), .in_2(in_17), .in_3(full_adder_7_out_5), .out_4(out_25), .out_5(out_26));
endmodule

module mux (
  input  A,
  input  connector,
  input  B,
  output out_4
);

  wire and_1_out, and_2_out, nand_1_out;

  nand nand_1 (nand_1_out, A, connector);
  and and_1 (and_1_out, connector, B);
  and and_2 (and_2_out, A, nand_1_out);
  or or_1 (out_4, and_2_out, and_1_out);
endmodule

module _8_bit_mux (
  input  in_1,
  input  [7:0] in_2,
  input  [7:0] in_3,
  output [7:0] out_4
);

  mux mux_1 (.A(in_2[0]), .connector(in_1), .B(in_3[0]), .out_4(out_4[0]));
  mux mux_2 (.A(in_2[1]), .connector(in_1), .B(in_3[1]), .out_4(out_4[1]));
  mux mux_3 (.A(in_2[2]), .connector(in_1), .B(in_3[2]), .out_4(out_4[2]));
  mux mux_4 (.A(in_2[3]), .connector(in_1), .B(in_3[3]), .out_4(out_4[3]));
  mux mux_5 (.A(in_2[4]), .connector(in_1), .B(in_3[4]), .out_4(out_4[4]));
  mux mux_6 (.A(in_2[5]), .connector(in_1), .B(in_3[5]), .out_4(out_4[5]));
  mux mux_7 (.A(in_2[6]), .connector(in_1), .B(in_3[6]), .out_4(out_4[6]));
  mux mux_8 (.A(in_2[7]), .connector(in_1), .B(in_3[7]), .out_4(out_4[7]));
endmodule

module _8_2_bit_mux (
  input  in_1,
  input  in_2,
  input  [7:0] in_3,
  input  [7:0] in_4,
  input  [7:0] in_5,
  input  [7:0] in_6,
  output [7:0] out_7
);

  wire [7:0] n8_bit_mux_1_out_4, n8_bit_mux_2_out_4;

  _8_bit_mux u_8_bit_mux_1 (.in_2(in_3), .in_3(in_4), .in_1(in_1), .out_4(n8_bit_mux_1_out_4));
  _8_bit_mux u_8_bit_mux_2 (.in_2(in_5), .in_3(in_6), .in_1(in_1), .out_4(n8_bit_mux_2_out_4));
  _8_bit_mux u_8_bit_mux_3 (.in_2(n8_bit_mux_1_out_4), .in_3(n8_bit_mux_2_out_4), .in_1(in_2), .out_4(out_7));
endmodule

module _8_3_bit_mux (
  input  in_1,
  input  in_2,
  input  in_3,
  input  [7:0] in_4,
  input  [7:0] in_5,
  input  [7:0] in_6,
  input  [7:0] in_7,
  input  [7:0] in_8,
  input  [7:0] in_9,
  input  [7:0] in_10,
  input  [7:0] in_11,
  output [7:0] out_12
);

  wire [7:0] n8_2_bit_mux_1_out_7, n8_2_bit_mux_2_out_7;

  _8_2_bit_mux u_8_2_bit_mux_1 (
    .in_3(in_4), .in_4(in_5), .in_5(in_6), .in_6(in_7), .in_1(in_1), .in_2(in_2), .out_7(n8_2_bit_mux_1_out_7));
  _8_2_bit_mux u_8_2_bit_mux_2 (
    .in_3(in_8), .in_4(in_9), .in_5(in_10), .in_6(in_11), .in_1(in_1), .in_2(in_2),
    .out_7(n8_2_bit_mux_2_out_7));
  _8_bit_mux u_8_bit_mux_1 (.in_2(n8_2_bit_mux_1_out_7), .in_3(n8_2_bit_mux_2_out_7), .in_1(in_3), .out_4(out_12));
endmodule
