// Logisim project full_thing.circ as structural Verilog: 1 circuit, main circuit main
module main (
);

  wire A_reg_p1;

  // Probe on A_reg_p1
  // bus_register A_reg: pin names not known; wires that end beside it: A_reg_p1, A_reg_p1, A_reg_p1, A_reg_p1
  // ALU CPU_ALU: pin names not known; wires that end beside it: A_reg_p1
endmodule
