// Logisim project fullthing.circ as structural Verilog: 20 circuits, main circuit main
module main (
);

  wire [7:0] alu_complete_1_status;

  ALU_complete alu_complete_1 (.status(alu_complete_1_status));  // open: A, B, op, outp
  bus_register bus_register_1 (.data_in(alu_complete_1_status));  // open: load, clock, data_out
endmodule

module ALU_complete (
  input  [3:0] op,
  input  [7:0] A,
  input  [7:0] B,
  output [7:0] outp,
  output [7:0] status
);

  wire [7:0] alu_1_out, shifter_unit_1_outp;

  SHIFTER_UNIT shifter_unit_1 (.A(A), .op(op[2:0]), .outp(shifter_unit_1_outp));
  ALU alu_1 (.A(A), .B(B), .OP(op[2:0]), .out(alu_1_out), .overflow(status[3]), .carry(status[4]));
  mux_8_bit mux_8_bit_1 (.in_2(shifter_unit_1_outp), .in_3(alu_1_out), .in_1(op[3]), .out_4(outp));
  nor nor_1 (status[1], outp[0], outp[1], outp[2], outp[3], outp[4], outp[5], outp[6], outp[7]);
  parity_check parity_check_1 (.in_1(outp), .out_2(status[0]));

  assign {status[7:5], status[2]} = {3'b000, outp[7]};

  // Notes on the sheet:
  //   0|0|0|carry|overflow|neg|zero|parity
endmodule

module SHIFTER_UNIT (
  input  [2:0] op,
  input  [7:0] A,
  output [7:0] outp
);

  mux_8_bit_3 mux_8_bit_3_1 (
    .in_4(A), .in_5({A[0], A[1], A[2], A[3], A[4], A[5], A[6], A[7]}), .in_6({A[6:0], A[0]}),
    .in_7({{2{A[7]}}, A[6:1]}), .in_8({A[6:0], A[7]}), .in_9({A[0], A[7:1]}), .in_10({A[6:0], 1'b0}),
    .in_11({1'b0, A[7:1]}), .in_1(op[0]), .in_2(op[1]), .in_3(op[2]), .out_12(outp));

  // Notes on the sheet:
  //   MIR
  //   AS
  //   RT
  //   LT
endmodule

module ALU (
  input  [2:0] OP,
  input  [7:0] A,
  input  [7:0] B,
  output overflow,
  output carry,
  output [7:0] out
);

  wire [7:0] add_sub_1_out, and_1_out, mux_8_bit_1_out_4, not_1_out, or_1_out, xor_1_out;

  mux_8_bit mux_8_bit_1 (.in_2(B), .in_3(8'h1), .in_1(OP[1]), .out_4(mux_8_bit_1_out_4));
  assign not_1_out = ~A;  // NOT_Gate not_1, 8 bits wide
  ADD_SUB add_sub_1 (.A(A), .B(mux_8_bit_1_out_4), .op(OP[0]), .out(add_sub_1_out), .overflow(overflow), .carry(carry));
  assign and_1_out = A & B;  // AND_Gate and_1, 8 bits wide
  assign or_1_out = A | B;  // OR_Gate or_1, 8 bits wide
  assign xor_1_out = A ^ B;  // XOR_Gate xor_1, 8 bits wide
  mux_8_bit_3 mux (
    .in_4(add_sub_1_out), .in_5(add_sub_1_out), .in_6(add_sub_1_out), .in_7(add_sub_1_out), .in_8(not_1_out),
    .in_9(and_1_out), .in_10(or_1_out), .in_11(xor_1_out), .in_1(OP[0]), .in_2(OP[1]), .in_3(OP[2]),
    .out_12(out));

  // Notes on the sheet:
  //   0|0|0|neg|carry|overflow|zero|parity
endmodule

module ADD_SUB (
  input  [7:0] B,
  input  op,
  input  [7:0] A,
  output [7:0] out,
  output overflow,
  output carry
);

  wire and_1_out, and_2_out, not_1_out, not_2_out, not_3_out;
  wire [7:0] xor_1_out;

  assign xor_1_out = B ^ {8{op}};  // XOR_Gate xor_1, 8 bits wide
  adder_8_bit full_adder_8_bit (
    .in_2(xor_1_out[0]), .in_3(xor_1_out[1]), .in_4(xor_1_out[2]), .in_5(xor_1_out[3]), .in_6(xor_1_out[4]),
    .in_7(xor_1_out[5]), .in_8(xor_1_out[6]), .in_9(xor_1_out[7]), .in_10(A[0]), .in_11(A[1]), .in_12(A[2]),
    .in_13(A[3]), .in_14(A[4]), .in_15(A[5]), .in_16(A[6]), .in_17(A[7]), .in_1(op), .out_18(out[0]),
    .out_19(out[1]), .out_20(out[2]), .out_21(out[3]), .out_22(out[4]), .out_23(out[5]), .out_24(out[6]),
    .out_25(out[7]), .out_26(carry));
  not not_1 (not_1_out, A[7]);
  not not_2 (not_2_out, out[7]);
  and and_1 (and_1_out, not_1_out, out[7], not_3_out);
  not not_3 (not_3_out, xor_1_out[7]);
  and and_2 (and_2_out, A[7], not_2_out, xor_1_out[7]);
  or or_1 (overflow, and_1_out, and_2_out);
endmodule

module adder_8_bit (
  input  in_1,
  input  in_2,
  input  in_3,
  input  in_4,
  input  in_5,
  input  in_6,
  input  in_7,
  input  in_8,
  input  in_9,
  input  in_10,
  input  in_11,
  input  in_12,
  input  in_13,
  input  in_14,
  input  in_15,
  input  in_16,
  input  in_17,
  output out_18,
  output out_19,
  output out_20,
  output out_21,
  output out_22,
  output out_23,
  output out_24,
  output out_25,
  output out_26
);

  wire fulladder1_out_5, fulladder2_out_5, fulladder3_out_5, fulladder4_out_5, fulladder5_out_5,
       fulladder6_out_5, fulladder7_out_5;

  full_adder fulladder1 (.in_1(in_2), .in_2(in_10), .in_3(in_1), .out_4(out_18), .out_5(fulladder1_out_5));
  full_adder fulladder2 (.in_1(in_3), .in_2(in_11), .in_3(fulladder1_out_5), .out_4(out_19), .out_5(fulladder2_out_5));
  full_adder fulladder3 (.in_1(in_4), .in_2(in_12), .in_3(fulladder2_out_5), .out_4(out_20), .out_5(fulladder3_out_5));
  full_adder fulladder4 (.in_1(in_5), .in_2(in_13), .in_3(fulladder3_out_5), .out_4(out_21), .out_5(fulladder4_out_5));
  full_adder fulladder5 (.in_1(in_6), .in_2(in_14), .in_3(fulladder4_out_5), .out_4(out_22), .out_5(fulladder5_out_5));
  full_adder fulladder6 (.in_1(in_7), .in_2(in_15), .in_3(fulladder5_out_5), .out_4(out_23), .out_5(fulladder6_out_5));
  full_adder fulladder7 (.in_1(in_8), .in_2(in_16), .in_3(fulladder6_out_5), .out_4(out_24), .out_5(fulladder7_out_5));
  full_adder fulladder8 (.in_1(in_9), .in_2(in_17), .in_3(fulladder7_out_5), .out_4(out_25), .out_5(out_26));
endmodule

module full_adder (
  input  in_1,
  input  in_2,
  input  in_3,
  output out_4,
  output out_5
);

  wire and_1_out, and_2_out, xor_1_out;

  xor xor_1 (xor_1_out, in_1, in_2);
  xor xor_2 (out_4, xor_1_out, in_3);
  and and_1 (and_1_out, xor_1_out, in_3);
  and and_2 (and_2_out, in_1, in_2);
  or or_1 (out_5, and_1_out, and_2_out);
endmodule

module mux (
  input  A,
  input  connector,
  input  B,
  output out_4
);

  wire and_1_out, and_2_out, nand_1_out;

  nand nand_1 (nand_1_out, A, connector);
  and and_1 (and_1_out, connector, B);
  and and_2 (and_2_out, A, nand_1_out);
  or or_1 (out_4, and_2_out, and_1_out);
endmodule

module mux_8_bit (
  input  in_1,
  input  [7:0] in_2,
  input  [7:0] in_3,
  output [7:0] out_4
);

  mux mux1 (.A(in_2[0]), .connector(in_1), .B(in_3[0]), .out_4(out_4[0]));
  mux mux2 (.A(in_2[1]), .connector(in_1), .B(in_3[1]), .out_4(out_4[1]));
  mux mux3 (.A(in_2[2]), .connector(in_1), .B(in_3[2]), .out_4(out_4[2]));
  mux mux4 (.A(in_2[3]), .connector(in_1), .B(in_3[3]), .out_4(out_4[3]));
  mux mux5 (.A(in_2[4]), .connector(in_1), .B(in_3[4]), .out_4(out_4[4]));
  mux mux6 (.A(in_2[5]), .connector(in_1), .B(in_3[5]), .out_4(out_4[5]));
  mux mux7 (.A(in_2[6]), .connector(in_1), .B(in_3[6]), .out_4(out_4[6]));
  mux mux8 (.A(in_2[7]), .connector(in_1), .B(in_3[7]), .out_4(out_4[7]));
endmodule

module mux_8_bit_2 (
  input  in_1,
  input  in_2,
  input  [7:0] in_3,
  input  [7:0] in_4,
  input  [7:0] in_5,
  input  [7:0] in_6,
  output [7:0] out_7
);

  wire [7:0] mux1_out_4, mux3_out_4;

  mux_8_bit mux1 (.in_2(in_3), .in_3(in_4), .in_1(in_1), .out_4(mux1_out_4));
  mux_8_bit mux3 (.in_2(in_5), .in_3(in_6), .in_1(in_1), .out_4(mux3_out_4));
  mux_8_bit mux2 (.in_2(mux1_out_4), .in_3(mux3_out_4), .in_1(in_2), .out_4(out_7));
endmodule

module mux_8_bit_3 (
  input  in_1,
  input  in_2,
  input  in_3,
  input  [7:0] in_4,
  input  [7:0] in_5,
  input  [7:0] in_6,
  input  [7:0] in_7,
  input  [7:0] in_8,
  input  [7:0] in_9,
  input  [7:0] in_10,
  input  [7:0] in_11,
  output [7:0] out_12
);

  wire [7:0] mux1_out_7, mux3_out_7;

  mux_8_bit_2 mux1 (.in_3(in_4), .in_4(in_5), .in_5(in_6), .in_6(in_7), .in_1(in_1), .in_2(in_2), .out_7(mux1_out_7));
  mux_8_bit_2 mux3 (.in_3(in_8), .in_4(in_9), .in_5(in_10), .in_6(in_11), .in_1(in_1), .in_2(in_2), .out_7(mux3_out_7));
  mux_8_bit mux2 (.in_2(mux1_out_7), .in_3(mux3_out_7), .in_1(in_3), .out_4(out_12));
endmodule

module mux_8_bit_4 (
  input  choose_3,
  input  choose_2,
  input  choose_1,
  input  choose_0,
  input  [7:0] out_0,
  input  [7:0] out_1,
  input  [7:0] out_2,
  input  [7:0] out_3,
  input  [7:0] out_4,
  input  [7:0] out_5,
  input  [7:0] out_6,
  input  [7:0] out_7,
  input  [7:0] out_8,
  input  [7:0] out_9,
  input  [7:0] out_10,
  input  [7:0] out_11,
  input  [7:0] out_12,
  input  [7:0] out_13,
  input  [7:0] out_14,
  input  [7:0] out_15,
  output [7:0] out_21
);

  wire [7:0] mux_1_out_12, mux_2_out_12;

  mux_8_bit_3 mux_1 (
    .in_4(out_0), .in_5(out_1), .in_6(out_2), .in_7(out_3), .in_8(out_4), .in_9(out_5), .in_10(out_6),
    .in_11(out_7), .in_1(choose_0), .in_2(choose_1), .in_3(choose_2), .out_12(mux_1_out_12));
  mux_8_bit_3 mux_2 (
    .in_4(out_8), .in_5(out_9), .in_6(out_10), .in_7(out_11), .in_8(out_12), .in_9(out_13), .in_10(out_14),
    .in_11(out_15), .in_1(choose_0), .in_2(choose_1), .in_3(choose_2), .out_12(mux_2_out_12));
  mux_8_bit mux_3 (.in_2(mux_1_out_12), .in_3(mux_2_out_12), .in_1(choose_3), .out_4(out_21));
endmodule

module bit_select_2_bit (
  input  in_1,
  input  in_2,
  output out_3,
  output out_4,
  output out_5,
  output out_6
);

  wire not_1_out, not_2_out, not_3_out;

  not not_1 (not_1_out, in_1);
  not not_2 (not_2_out, in_2);
  not not_3 (not_3_out, in_1);
  and and_1 (out_3, not_1_out, not_2_out);
  and and_2 (out_5, not_3_out, in_2);
  and and_3 (out_6, in_1, in_2);
  and and_4 (out_4, not_2_out, in_1);
endmodule

module bit_select_3_bit (
  input  in_1,
  input  in_2,
  input  in_3,
  output out_4,
  output out_5,
  output out_6,
  output out_7,
  output out_8,
  output out_9,
  output out_10,
  output out_11
);

  wire bit_select_2_bit_1_out_3, bit_select_2_bit_1_out_4, bit_select_2_bit_1_out_5,
       bit_select_2_bit_1_out_6, not_1_out;

  bit_select_2_bit bit_select_2_bit_1 (
    .in_1(in_1), .in_2(in_2), .out_3(bit_select_2_bit_1_out_3), .out_4(bit_select_2_bit_1_out_4),
    .out_5(bit_select_2_bit_1_out_5), .out_6(bit_select_2_bit_1_out_6));
  not not_1 (not_1_out, in_3);
  and and_1 (out_4, bit_select_2_bit_1_out_3, not_1_out);
  and and_2 (out_5, bit_select_2_bit_1_out_4, not_1_out);
  and and_3 (out_6, bit_select_2_bit_1_out_5, not_1_out);
  and and_4 (out_7, bit_select_2_bit_1_out_6, not_1_out);
  and and_5 (out_8, bit_select_2_bit_1_out_3, in_3);
  and and_6 (out_9, bit_select_2_bit_1_out_4, in_3);
  and and_7 (out_10, bit_select_2_bit_1_out_5, in_3);
  and and_8 (out_11, bit_select_2_bit_1_out_6, in_3);
endmodule

module latch1 (
  input  in_1,
  input  in_2,
  output out_3,
  output out_4
);

  wire nand_1_out, nand_2_out, not_1_out;

  not not_1 (not_1_out, in_1);
  nand nand_1 (nand_1_out, in_1, in_2);
  nand nand_2 (nand_2_out, in_2, not_1_out);
  nor nor_1 (out_3, nand_1_out, out_4);
  nor nor_2 (out_4, out_3, nand_2_out);
endmodule

module d_flipflop (
  input  value,
  input  enable,
  output Q,
  output QB
);

  wire nand_1_out, nand_2_out, not_1_out;

  not not_1 (not_1_out, value);
  nand nand_1 (nand_1_out, value, enable);
  nand nand_2 (nand_2_out, enable, not_1_out);
  nand nand_3 (Q, nand_1_out, QB);
  nand nand_4 (QB, Q, nand_2_out);
endmodule

module bus_register (
  input  [7:0] data_in,
  input  load,
  input  clock,
  output [7:0] data_out
);

  wire and_1_out;

  and and_1 (and_1_out, load, clock);
  d_flipflop d_flipflop_1 (.value(data_in[7]), .enable(and_1_out), .Q(data_out[7]));  // open: QB
  d_flipflop d_flipflop_2 (.value(data_in[6]), .enable(and_1_out), .Q(data_out[6]));  // open: QB
  d_flipflop d_flipflop_3 (.value(data_in[5]), .enable(and_1_out), .Q(data_out[5]));  // open: QB
  d_flipflop d_flipflop_4 (.value(data_in[4]), .enable(and_1_out), .Q(data_out[4]));  // open: QB
  d_flipflop d_flipflop_5 (.value(data_in[3]), .enable(and_1_out), .Q(data_out[3]));  // open: QB
  d_flipflop d_flipflop_6 (.value(data_in[2]), .enable(and_1_out), .Q(data_out[2]));  // open: QB
  d_flipflop d_flipflop_7 (.value(data_in[1]), .enable(and_1_out), .Q(data_out[1]));  // open: QB
  d_flipflop d_flipflop_8 (.value(data_in[0]), .enable(and_1_out), .Q(data_out[0]));  // open: QB
endmodule

module parity_check (
  input  [7:0] in_1,
  output out_2
);

  wire xnor_1_out, xnor_2_out, xnor_3_out, xnor_4_out, xnor_5_out, xnor_6_out;

  xnor xnor_1 (xnor_1_out, in_1[0], in_1[1]);
  xnor xnor_2 (xnor_2_out, in_1[2], in_1[3]);
  xnor xnor_3 (xnor_3_out, in_1[4], in_1[5]);
  xnor xnor_4 (xnor_4_out, in_1[6], in_1[7]);
  xnor xnor_5 (xnor_5_out, xnor_1_out, xnor_2_out);
  xnor xnor_6 (xnor_6_out, xnor_3_out, xnor_4_out);
  xnor xnor_7 (out_2, xnor_5_out, xnor_6_out);

  // Notes on the sheet:
  //   odd = 0
  //   even = 1
endmodule

module reg_interface (
  input  reset,
  input  clock,
  input  [2:0] in_3,
  input  [2:0] load_a,
  input  [7:0] in_5,
  input  [7:0] in_6,
  input  [7:0] in_7,
  input  [7:0] in_8,
  input  [7:0] in_9,
  input  [2:0] load_b,
  input  [7:0] in_11,
  input  [7:0] in_12,
  input  [7:0] in_13
);

  wire bit_select_3_bit_1_out_4, bit_select_3_bit_1_out_5, bit_select_3_bit_1_out_6,
       bit_select_3_bit_1_out_7, bit_select_3_bit_1_out_8, bit_select_3_bit_1_out_9,
       bit_select_3_bit_1_out_10, bit_select_3_bit_1_out_11, or_1_out, or_2_out, or_3_out, or_4_out,
       or_5_out, or_6_out, or_7_out, or_8_out, or_9_out, pulse_module_1_a_out, pulse_module_2_a_out;
  wire [7:0] bus_register_1_data_out, bus_register_2_data_out, bus_register_3_data_out,
       bus_register_4_data_out, bus_register_5_data_out, bus_register_6_data_out, bus_register_7_data_out,
       bus_register_8_data_out, mux_8_bit_1_out_4, mux_8_bit_2_out_4, mux_8_bit_3_out_4, mux_8_bit_4_out_4,
       mux_8_bit_5_out_4, mux_8_bit_6_out_4, mux_8_bit_7_out_4, mux_8_bit_8_out_4;

  mux_8_bit mux_8_bit_1 (.in_2(in_5), .in_3({8{1'b0}}), .in_1(reset), .out_4(mux_8_bit_1_out_4));
  mux_8_bit mux_8_bit_2 (.in_2(in_6), .in_3({8{1'b0}}), .in_1(reset), .out_4(mux_8_bit_2_out_4));
  mux_8_bit mux_8_bit_3 (.in_2(in_7), .in_3({8{1'b0}}), .in_1(reset), .out_4(mux_8_bit_3_out_4));
  mux_8_bit mux_8_bit_4 (.in_2(in_8), .in_3({8{1'b0}}), .in_1(reset), .out_4(mux_8_bit_4_out_4));
  mux_8_bit mux_8_bit_5 (.in_2(in_9), .in_3({8{1'b0}}), .in_1(reset), .out_4(mux_8_bit_5_out_4));
  mux_8_bit mux_8_bit_6 (.in_2(in_11), .in_3({8{1'b0}}), .in_1(reset), .out_4(mux_8_bit_6_out_4));
  mux_8_bit mux_8_bit_7 (.in_2(in_12), .in_3({8{1'b0}}), .in_1(reset), .out_4(mux_8_bit_7_out_4));
  mux_8_bit mux_8_bit_8 (.in_2(in_13), .in_3({8{1'b0}}), .in_1(reset), .out_4(mux_8_bit_8_out_4));
  bit_select_3_bit bit_select_3_bit_1 (
    .in_1(in_3[0]), .in_2(in_3[1]), .in_3(in_3[2]), .out_4(bit_select_3_bit_1_out_4),
    .out_5(bit_select_3_bit_1_out_5), .out_6(bit_select_3_bit_1_out_6), .out_7(bit_select_3_bit_1_out_7),
    .out_8(bit_select_3_bit_1_out_8), .out_9(bit_select_3_bit_1_out_9), .out_10(bit_select_3_bit_1_out_10),
    .out_11(bit_select_3_bit_1_out_11));
  pulse_module pulse_module_1 (.A(reset), .A_out(pulse_module_1_a_out));
  or or_1 (or_1_out, pulse_module_1_a_out, clock);
  bus_register bus_register_1 (
    .data_in(mux_8_bit_1_out_4), .load(or_2_out), .clock(pulse_module_2_a_out),
    .data_out(bus_register_1_data_out));
  pulse_module pulse_module_2 (.A(or_1_out), .A_out(pulse_module_2_a_out));
  or or_2 (or_2_out, reset, bit_select_3_bit_1_out_4);
  bus_register bus_register_2 (
    .data_in(mux_8_bit_2_out_4), .load(or_3_out), .clock(pulse_module_2_a_out),
    .data_out(bus_register_2_data_out));
  or or_3 (or_3_out, reset, bit_select_3_bit_1_out_5);
  bus_register bus_register_3 (
    .data_in(mux_8_bit_3_out_4), .load(or_4_out), .clock(pulse_module_2_a_out),
    .data_out(bus_register_3_data_out));
  or or_4 (or_4_out, reset, bit_select_3_bit_1_out_6);
  bus_register bus_register_4 (
    .data_in(mux_8_bit_4_out_4), .load(or_5_out), .clock(pulse_module_2_a_out),
    .data_out(bus_register_4_data_out));
  or or_5 (or_5_out, reset, bit_select_3_bit_1_out_7);
  bus_register bus_register_5 (
    .data_in(mux_8_bit_5_out_4), .load(or_6_out), .clock(pulse_module_2_a_out),
    .data_out(bus_register_5_data_out));
  or or_6 (or_6_out, reset, bit_select_3_bit_1_out_8);
  bus_register bus_register_6 (
    .data_in(mux_8_bit_6_out_4), .load(or_7_out), .clock(pulse_module_2_a_out),
    .data_out(bus_register_6_data_out));
  or or_7 (or_7_out, reset, bit_select_3_bit_1_out_9);
  bus_register bus_register_7 (
    .data_in(mux_8_bit_7_out_4), .load(or_8_out), .clock(pulse_module_2_a_out),
    .data_out(bus_register_7_data_out));
  or or_8 (or_8_out, reset, bit_select_3_bit_1_out_10);
  bus_register bus_register_8 (
    .data_in(mux_8_bit_8_out_4), .load(or_9_out), .clock(pulse_module_2_a_out),
    .data_out(bus_register_8_data_out));
  or or_9 (or_9_out, reset, bit_select_3_bit_1_out_11);
  // Probe on bus_register_1_data_out
  // Probe on bus_register_2_data_out
  // Probe on bus_register_3_data_out
  // Probe on bus_register_4_data_out
  // Probe on bus_register_5_data_out
  // Probe on bus_register_6_data_out
  // Probe on bus_register_7_data_out
  // Probe on bus_register_8_data_out
  mux_8_bit_3 mux_8_bit_3_1 (
    .in_4(bus_register_1_data_out), .in_5(bus_register_2_data_out), .in_6(bus_register_3_data_out),
    .in_7(bus_register_4_data_out), .in_8(bus_register_5_data_out), .in_9(bus_register_6_data_out),
    .in_10(bus_register_7_data_out), .in_11(bus_register_8_data_out), .in_1(load_a[0]), .in_2(load_a[1]),
    .in_3(load_a[2]));  // open: out_12
  mux_8_bit_3 mux_8_bit_3_2 (
    .in_4(bus_register_1_data_out), .in_5(bus_register_2_data_out), .in_6(bus_register_3_data_out),
    .in_7(bus_register_4_data_out), .in_8(bus_register_5_data_out), .in_9(bus_register_6_data_out),
    .in_10(bus_register_7_data_out), .in_11(bus_register_8_data_out), .in_1(load_b[0]), .in_2(load_b[1]),
    .in_3(load_b[2]));  // open: out_12
endmodule

module pulse_module (
  input  A,
  output A_out
);

  wire buffer_1_out, nand_1_out, not_1_out;

  buf buffer_1 (buffer_1_out, A);
  not not_1 (not_1_out, buffer_1_out);
  nand nand_1 (nand_1_out, A, not_1_out);
  not not_2 (A_out, nand_1_out);
endmodule
