// Logisim project registers.circ as structural Verilog: 3 circuits, main circuit latch1
module latch1 (
  input  in_1,
  input  in_2,
  output out_3,
  output out_4
);

  wire nand_1_out, nand_2_out, not_1_out;

  not not_1 (not_1_out, in_1);
  nand nand_1 (nand_1_out, in_1, in_2);
  nand nand_2 (nand_2_out, in_2, not_1_out);
  nor nor_1 (out_3, nand_1_out, out_4);
  nor nor_2 (out_4, out_3, nand_2_out);
endmodule

module pulse_d_flipflop (
  input  value,
  input  enable,
  output Q,
  output QB
);

  wire buffer_1_out, nand_1_out, nand_2_out, nand_3_out, not_1_out, not_2_out, not_3_out;

  buf buffer_1 (buffer_1_out, enable);
  not not_1 (not_1_out, buffer_1_out);
  nand nand_1 (nand_1_out, enable, not_1_out);
  not not_2 (not_2_out, nand_1_out);
  not not_3 (not_3_out, value);
  nand nand_2 (nand_2_out, value, not_2_out);
  nand nand_3 (nand_3_out, not_2_out, not_3_out);
  nand nand_4 (Q, nand_2_out, QB);
  nand nand_5 (QB, Q, nand_3_out);
endmodule

module bus_register (
  input  [7:0] data_in,
  input  load,
  input  clock,
  input  enable,
  output [7:0] data_out
);

  wire and_1_out, pulse_d_flipflop_1_q, pulse_d_flipflop_2_q, pulse_d_flipflop_3_q, pulse_d_flipflop_4_q,
       pulse_d_flipflop_5_q, pulse_d_flipflop_6_q, pulse_d_flipflop_7_q, pulse_d_flipflop_8_q;

  and and_1 (and_1_out, load, clock);
  pulse_d_flipflop pulse_d_flipflop_1 (.value(data_in[7]), .enable(and_1_out), .Q(pulse_d_flipflop_1_q));  // open: QB
  and and_2 (data_out[7], pulse_d_flipflop_1_q, enable);
  pulse_d_flipflop pulse_d_flipflop_2 (.value(data_in[6]), .enable(and_1_out), .Q(pulse_d_flipflop_2_q));  // open: QB
  and and_3 (data_out[6], pulse_d_flipflop_2_q, enable);
  and and_4 (data_out[5], pulse_d_flipflop_3_q, enable);
  pulse_d_flipflop pulse_d_flipflop_3 (.value(data_in[5]), .enable(and_1_out), .Q(pulse_d_flipflop_3_q));  // open: QB
  and and_5 (data_out[4], pulse_d_flipflop_4_q, enable);
  pulse_d_flipflop pulse_d_flipflop_4 (.value(data_in[4]), .enable(and_1_out), .Q(pulse_d_flipflop_4_q));  // open: QB
  and and_6 (data_out[3], pulse_d_flipflop_5_q, enable);
  pulse_d_flipflop pulse_d_flipflop_5 (.value(data_in[3]), .enable(and_1_out), .Q(pulse_d_flipflop_5_q));  // open: QB
  and and_7 (data_out[2], pulse_d_flipflop_6_q, enable);
  pulse_d_flipflop pulse_d_flipflop_6 (.value(data_in[2]), .enable(and_1_out), .Q(pulse_d_flipflop_6_q));  // open: QB
  and and_8 (data_out[1], pulse_d_flipflop_7_q, enable);
  pulse_d_flipflop pulse_d_flipflop_7 (.value(data_in[1]), .enable(and_1_out), .Q(pulse_d_flipflop_7_q));  // open: QB
  and and_9 (data_out[0], pulse_d_flipflop_8_q, enable);
  pulse_d_flipflop pulse_d_flipflop_8 (.value(data_in[0]), .enable(and_1_out), .Q(pulse_d_flipflop_8_q));  // open: QB
endmodule
